// Logisim project latches.circ as structural Verilog: 1 circuit, main circuit main
module main (
  output Q,
  output Q_2
);

  wire button_1_out, button_2_out, button_3_out, button_4_out, nand_1_out, nor_1_out, not_1_out, not_2_out;

  Button button_1 (.out(button_1_out));
  Button button_2 (.out(button_2_out));
  not not_1 (not_1_out, button_3_out);
  Button button_3 (.out(button_3_out));
  not not_2 (not_2_out, button_4_out);
  Button button_4 (.out(button_4_out));
  nor nor_1 (nor_1_out, button_2_out, Q);
  nand nand_1 (nand_1_out, not_2_out, Q_2);
  nor nor_2 (Q, button_1_out, nor_1_out);
  LED led_1 (.in(Q));
  nand nand_2 (Q_2, not_1_out, nand_1_out);
  LED led_2 (.in(Q_2));

  // Notes on the sheet:
  //   R
  //   S
  //   S
  //   R
  //   RS-NOR-latch with reset priority
  //   SR-NAND-latch with set priority
endmodule
