// Logisim project shifters.circ as structural Verilog: 2 circuits, main circuit right_shifter
module right_shifter (
  input  l,
  input  x7,
  input  x6,
  input  x5,
  input  x4,
  input  x3,
  input  x2,
  input  x1,
  input  x0,
  input  s0,
  input  s1,
  output y7,
  output y6,
  output y5,
  output y4,
  output y3,
  output y2,
  output y1,
  output y0
);

  wire multiplexer_1_out, multiplexer_3_out, multiplexer_5_out, multiplexer_7_out, multiplexer_9_out,
       multiplexer_11_out, multiplexer_13_out, multiplexer_15_out;

  LED led_1 (.in(x7));
  Multiplexer multiplexer_1 (.in0(x7), .in1(l), .out(multiplexer_1_out), .sel(s0));
  Multiplexer multiplexer_2 (.in0(multiplexer_1_out), .in1(l), .out(y7), .sel(s1));
  LED led_2 (.in(y7));
  LED led_3 (.in(x6));
  Multiplexer multiplexer_3 (.in0(x6), .in1(x7), .out(multiplexer_3_out), .sel(s0));
  Multiplexer multiplexer_4 (.in0(multiplexer_3_out), .in1(l), .out(y6), .sel(s1));
  LED led_4 (.in(y6));
  LED led_5 (.in(x5));
  Multiplexer multiplexer_5 (.in0(x5), .in1(x6), .out(multiplexer_5_out), .sel(s0));
  Multiplexer multiplexer_6 (.in0(multiplexer_5_out), .in1(multiplexer_1_out), .out(y5), .sel(s1));
  LED led_6 (.in(y5));
  LED led_7 (.in(x4));
  Multiplexer multiplexer_7 (.in0(x4), .in1(x5), .out(multiplexer_7_out), .sel(s0));
  Multiplexer multiplexer_8 (.in0(multiplexer_7_out), .in1(multiplexer_3_out), .out(y4), .sel(s1));
  LED led_8 (.in(y4));
  LED led_9 (.in(x3));
  Multiplexer multiplexer_9 (.in0(x3), .in1(x4), .out(multiplexer_9_out), .sel(s0));
  Multiplexer multiplexer_10 (.in0(multiplexer_9_out), .in1(multiplexer_5_out), .out(y3), .sel(s1));
  LED led_10 (.in(y3));
  LED led_11 (.in(x2));
  Multiplexer multiplexer_11 (.in0(x2), .in1(x3), .out(multiplexer_11_out), .sel(s0));
  Multiplexer multiplexer_12 (.in0(multiplexer_11_out), .in1(multiplexer_7_out), .out(y2), .sel(s1));
  LED led_12 (.in(y2));
  LED led_13 (.in(x1));
  Multiplexer multiplexer_13 (.in0(x1), .in1(x2), .out(multiplexer_13_out), .sel(s0));
  Multiplexer multiplexer_14 (.in0(multiplexer_13_out), .in1(multiplexer_9_out), .out(y1), .sel(s1));
  LED led_14 (.in(y1));
  LED led_15 (.in(x0));
  Multiplexer multiplexer_15 (.in0(x0), .in1(x1), .out(multiplexer_15_out), .sel(s0));
  Multiplexer multiplexer_16 (.in0(multiplexer_15_out), .in1(multiplexer_11_out), .out(y0), .sel(s1));
  LED led_16 (.in(y0));

  // Notes on the sheet:
  //   8-bit Barrel Shifter
  //   Shift right by up to 3 positions
  //   Use 'L' input to switch between logical (0) and arithmetic (sign bit) shifting
endmodule

module bidirectional_shifter (
  input  x7,
  input  x6,
  input  x5,
  input  x4,
  input  x3,
  input  x2,
  input  x1,
  input  x0,
  input  dir,
  input  s0,
  input  l,
  input  s1,
  output out_13,
  output out_14,
  output out_15,
  output out_16,
  output out_17,
  output out_18,
  output out_19,
  output out_20
);

  wire multiplexer_1_out, multiplexer_2_out, multiplexer_5_out, multiplexer_6_out, multiplexer_8_out,
       multiplexer_11_out, multiplexer_12_out, multiplexer_15_out, right_shifter_1_y0, right_shifter_1_y1,
       right_shifter_1_y2, right_shifter_1_y3, right_shifter_1_y4, right_shifter_1_y5, right_shifter_1_y6,
       right_shifter_1_y7;

  LED led_1 (.in(x6));
  LED led_2 (.in(x7));
  Multiplexer multiplexer_1 (.in0(x6), .in1(x1), .out(multiplexer_1_out), .sel(dir));
  Multiplexer multiplexer_2 (.in0(x7), .in1(x0), .out(multiplexer_2_out), .sel(dir));
  Multiplexer multiplexer_3 (.in0(right_shifter_1_y6), .in1(right_shifter_1_y1), .out(out_14), .sel(dir));
  Multiplexer multiplexer_4 (.in0(right_shifter_1_y7), .in1(right_shifter_1_y0), .out(out_13), .sel(dir));
  LED led_3 (.in(out_13));
  LED led_4 (.in(out_14));
  LED led_5 (.in(x5));
  LED led_6 (.in(x4));
  Multiplexer multiplexer_5 (.in0(x5), .in1(x2), .out(multiplexer_5_out), .sel(dir));
  Multiplexer multiplexer_6 (.in0(x4), .in1(x3), .out(multiplexer_6_out), .sel(dir));
  Multiplexer multiplexer_7 (.in0(right_shifter_1_y5), .in1(right_shifter_1_y2), .out(out_15), .sel(dir));
  LED led_7 (.in(out_15));
  LED led_8 (.in(x3));
  Multiplexer multiplexer_8 (.in0(x3), .in1(x4), .out(multiplexer_8_out), .sel(dir));
  right_shifter right_shifter_1 (
    .x7(multiplexer_2_out), .x6(multiplexer_1_out), .x5(multiplexer_5_out), .x4(multiplexer_6_out),
    .x3(multiplexer_8_out), .l(l), .x2(multiplexer_11_out), .x1(multiplexer_12_out), .x0(multiplexer_15_out),
    .s0(s0), .s1(s1), .y7(right_shifter_1_y7), .y6(right_shifter_1_y6), .y5(right_shifter_1_y5),
    .y4(right_shifter_1_y4), .y3(right_shifter_1_y3), .y2(right_shifter_1_y2), .y1(right_shifter_1_y1),
    .y0(right_shifter_1_y0));
  Multiplexer multiplexer_9 (.in0(right_shifter_1_y4), .in1(right_shifter_1_y3), .out(out_16), .sel(dir));
  Multiplexer multiplexer_10 (.in0(right_shifter_1_y3), .in1(right_shifter_1_y4), .out(out_17), .sel(dir));
  LED led_9 (.in(out_16));
  LED led_10 (.in(out_17));
  LED led_11 (.in(x2));
  LED led_12 (.in(x1));
  Multiplexer multiplexer_11 (.in0(x2), .in1(x5), .out(multiplexer_11_out), .sel(dir));
  Multiplexer multiplexer_12 (.in0(x1), .in1(x6), .out(multiplexer_12_out), .sel(dir));
  Multiplexer multiplexer_13 (.in0(right_shifter_1_y2), .in1(right_shifter_1_y5), .out(out_18), .sel(dir));
  Multiplexer multiplexer_14 (.in0(right_shifter_1_y1), .in1(right_shifter_1_y6), .out(out_19), .sel(dir));
  LED led_13 (.in(out_18));
  LED led_14 (.in(x0));
  Multiplexer multiplexer_15 (.in0(x0), .in1(x7), .out(multiplexer_15_out), .sel(dir));
  Multiplexer multiplexer_16 (.in0(right_shifter_1_y0), .in1(right_shifter_1_y7), .out(out_20), .sel(dir));
  LED led_15 (.in(out_19));
  LED led_16 (.in(out_20));

  // Notes on the sheet:
  //   Bidirectional 8-bit barrel shifter
  //   0 = right, 1 = left
  //   arithmetic (sign bit) shift
  //   Shift up to 3 positions, specifiy direction with 'dir'
  //   Use 'L' input to switch between logical (0) and
endmodule
