// Logisim project week10.circ as structural Verilog: 1 circuit, main circuit main
module main (
  input  W,
  input  reset,
  output Z
);

  wire and_1_out, and_2_out, clk_out, d_ff_1_q, d_ff_1_qn, d_ff_2_q, d_ff_2_qn, or_1_out, xor_1_out,
       xor_2_out;

  Clock clk (.out(clk_out));
  xor xor_1 (xor_1_out, W, xor_2_out);
  and and_1 (and_1_out, d_ff_1_qn, d_ff_2_qn);
  and and_2 (and_2_out, W, d_ff_2_q);
  xor xor_2 (xor_2_out, d_ff_2_q, d_ff_1_q);
  D_Flip_Flop d_ff_1 (.D(xor_1_out), .clk(clk_out), .Q(d_ff_1_q), .Qn(d_ff_1_qn), .reset(reset));  // open: preset
  D_Flip_Flop d_ff_2 (.D(or_1_out), .clk(clk_out), .Q(d_ff_2_q), .Qn(d_ff_2_qn), .reset(reset));  // open: preset
  or or_1 (or_1_out, and_1_out, and_2_out);
  and and_3 (Z, d_ff_1_q, d_ff_2_q);

  // Notes on the sheet:
  //   Z = y2 y1
  //   Y1 = W(!(y2 xor y1)) + !W(y2 xor y1)
  //   Y2 = !y2 !y1 + W(y2 !y1 + y2 y1)
endmodule
