// Logisim project week5_adders.circ as structural Verilog: 7 circuits, main circuit HalfAdder
module HalfAdder (
  input  X,
  input  Y,
  output S,
  output C
);

  xor xor_1 (S, X, Y);
  and and_1 (C, X, Y);
endmodule

module FullAdder (
  input  Ci,
  input  Xi,
  input  Yi,
  output Si,
  output Ci_1
);

  wire halfadder_1_c, halfadder_1_s, halfadder_2_c;

  HalfAdder halfadder_1 (.X(Xi), .Y(Yi), .S(halfadder_1_s), .C(halfadder_1_c));
  HalfAdder halfadder_2 (.X(Ci), .Y(halfadder_1_s), .S(Si), .C(halfadder_2_c));
  or or_1 (Ci_1, halfadder_2_c, halfadder_1_c);
endmodule

module FourBitRippleCarryAdder (
  input  Y0,
  input  Y1,
  input  Y2,
  input  Y3,
  input  X0,
  input  X1,
  input  X2,
  input  X3,
  output S0,
  output S1,
  output S2,
  output S3,
  output C4
);

  wire fulladder_1_ci_1, fulladder_2_ci_1, fulladder_3_ci_1;

  FullAdder fulladder_1 (.Ci(1'b0), .Xi(X0), .Yi(Y0), .Si(S0), .Ci_1(fulladder_1_ci_1));
  FullAdder fulladder_2 (.Ci(fulladder_1_ci_1), .Xi(X1), .Yi(Y1), .Si(S1), .Ci_1(fulladder_2_ci_1));
  FullAdder fulladder_3 (.Ci(fulladder_2_ci_1), .Xi(X2), .Yi(Y2), .Si(S2), .Ci_1(fulladder_3_ci_1));
  FullAdder fulladder_4 (.Ci(fulladder_3_ci_1), .Xi(X3), .Yi(Y3), .Si(S3), .Ci_1(C4));

  // Notes on the sheet:
  //   Worst case gate delay: 48 ns
endmodule

module SevenSegmentWired (
  input  W,
  input  X,
  input  Y,
  input  Z,
  output a,
  output b,
  output c,
  output d,
  output e,
  output f,
  output g
);

  wire and_1_out, and_2_out, and_3_out, and_4_out, and_5_out, and_6_out, or_1_out, or_2_out, xor_1_out,
       xor_2_out;

  xor xor_1 (xor_1_out, X, Z);
  xor xor_2 (xor_2_out, Y, Z);
  or or_1 (or_1_out, X, Z);
  and and_1 (and_1_out, ~X, Y);  // AND_Gate
  and and_2 (and_2_out, Y, ~Z);  // AND_Gate
  and and_3 (and_3_out, X, ~Y, Z);  // AND_Gate
  or or_2 (or_2_out, Y, Z);
  and and_4 (and_4_out, X, ~Y);  // AND_Gate
  and and_5 (and_5_out, X, ~Z);  // AND_Gate
  and and_6 (and_6_out, ~X, Y);  // AND_Gate
  or or_3 (a, W, Y, ~xor_1_out);  // OR_Gate
  or or_4 (b, ~X, ~xor_2_out);  // OR_Gate
  or or_5 (c, X, ~Y, Z);  // OR_Gate
  or or_6 (d, ~or_1_out, and_1_out, and_2_out, and_3_out, W);  // OR_Gate
  or or_7 (e, ~or_1_out, and_2_out);  // OR_Gate
  or or_8 (f, W, ~or_2_out, and_4_out, and_5_out);  // OR_Gate
  or or_9 (g, W, and_6_out, and_4_out, and_5_out);
  _7_Segment_Display #(.decimalPoint("false")) u_7_segment_display_1 (.g(g), .f(f), .a(a), .b(b), .e(e), .d(d), .c(c));

  // Notes on the sheet:
  //   Seven Segment Display
  //   with improved logic expressions for a-g
endmodule

module OneBitAddSub (
  input  OP,
  input  X,
  input  Y,
  output D,
  output B_out
);

  wire xor_1_out;

  xor xor_1 (xor_1_out, OP, Y);
  FullAdder fulladder_1 (.Ci(OP), .Xi(X), .Yi(xor_1_out), .Si(D), .Ci_1(B_out));
endmodule

module FourBitRippleCarryAddSub (
  input  X0,
  input  X1,
  input  X2,
  input  X3,
  input  Y0,
  input  Y1,
  input  Y2,
  input  Y3,
  input  OP,
  output S0,
  output S1,
  output S2,
  output S3,
  output C4
);

  wire fulladder_1_ci_1, fulladder_2_ci_1, fulladder_3_ci_1, xor_1_out, xor_2_out, xor_3_out, xor_4_out;

  xor xor_1 (xor_1_out, OP, Y0);
  FullAdder fulladder_1 (.Ci(OP), .Xi(X0), .Yi(xor_1_out), .Si(S0), .Ci_1(fulladder_1_ci_1));
  xor xor_2 (xor_2_out, OP, Y1);
  FullAdder fulladder_2 (.Ci(fulladder_1_ci_1), .Xi(X1), .Yi(xor_2_out), .Si(S1), .Ci_1(fulladder_2_ci_1));
  xor xor_3 (xor_3_out, OP, Y2);
  FullAdder fulladder_3 (.Ci(fulladder_2_ci_1), .Xi(X2), .Yi(xor_3_out), .Si(S2), .Ci_1(fulladder_3_ci_1));
  xor xor_4 (xor_4_out, OP, Y3);
  FullAdder fulladder_4 (.Ci(fulladder_3_ci_1), .Xi(X3), .Yi(xor_4_out), .Si(S3), .Ci_1(C4));
endmodule

module Main (
  input  in_1,
  input  in_2,
  input  in_3,
  input  in_4,
  input  in_5,
  input  in_6,
  input  in_7,
  input  in_8,
  input  in_9,
  input  in_10,
  input  in_11,
  input  in_12,
  input  in_13,
  input  in_14,
  input  in_15,
  input  in_16,
  input  OP,
  output out_18,
  output out_19
);

  wire fourbitripplecarryadder_1_s0, fourbitripplecarryadder_1_s1, fourbitripplecarryadder_1_s2,
       fourbitripplecarryadder_1_s3, fourbitripplecarryaddsub_1_s0, fourbitripplecarryaddsub_1_s1,
       fourbitripplecarryaddsub_1_s2, fourbitripplecarryaddsub_1_s3, sevensegmentwired_1_a,
       sevensegmentwired_1_b, sevensegmentwired_1_c, sevensegmentwired_1_d, sevensegmentwired_1_e,
       sevensegmentwired_1_f, sevensegmentwired_1_g, sevensegmentwired_2_a, sevensegmentwired_2_b,
       sevensegmentwired_2_c, sevensegmentwired_2_d, sevensegmentwired_2_e, sevensegmentwired_2_f,
       sevensegmentwired_2_g;

  FourBitRippleCarryAdder fourbitripplecarryadder_1 (
    .Y0(in_1), .Y1(in_2), .Y2(in_3), .Y3(in_4), .X0(in_5), .X1(in_6), .X2(in_7), .X3(in_8),
    .S0(fourbitripplecarryadder_1_s0), .S1(fourbitripplecarryadder_1_s1), .S2(fourbitripplecarryadder_1_s2),
    .S3(fourbitripplecarryadder_1_s3), .C4(out_18));
  FourBitRippleCarryAddSub fourbitripplecarryaddsub_1 (
    .X0(in_9), .X1(in_10), .X2(in_11), .X3(in_12), .Y0(in_13), .Y1(in_14), .Y2(in_15), .Y3(in_16), .OP(OP),
    .S0(fourbitripplecarryaddsub_1_s0), .S1(fourbitripplecarryaddsub_1_s1),
    .S2(fourbitripplecarryaddsub_1_s2), .S3(fourbitripplecarryaddsub_1_s3), .C4(out_19));
  SevenSegmentWired sevensegmentwired_1 (
    .W(fourbitripplecarryadder_1_s3), .X(fourbitripplecarryadder_1_s2), .Y(fourbitripplecarryadder_1_s1),
    .Z(fourbitripplecarryadder_1_s0), .a(sevensegmentwired_1_a), .b(sevensegmentwired_1_b),
    .c(sevensegmentwired_1_c), .d(sevensegmentwired_1_d), .e(sevensegmentwired_1_e),
    .f(sevensegmentwired_1_f), .g(sevensegmentwired_1_g));
  SevenSegmentWired sevensegmentwired_2 (
    .W(fourbitripplecarryaddsub_1_s3), .X(fourbitripplecarryaddsub_1_s2), .Y(fourbitripplecarryaddsub_1_s1),
    .Z(fourbitripplecarryaddsub_1_s0), .a(sevensegmentwired_2_a), .b(sevensegmentwired_2_b),
    .c(sevensegmentwired_2_c), .d(sevensegmentwired_2_d), .e(sevensegmentwired_2_e),
    .f(sevensegmentwired_2_f), .g(sevensegmentwired_2_g));
  _7_Segment_Display #(.decimalPoint("false")) u_7_segment_display_1 (
    .g(sevensegmentwired_1_g), .f(sevensegmentwired_1_f), .a(sevensegmentwired_1_a),
    .b(sevensegmentwired_1_b), .e(sevensegmentwired_1_e), .d(sevensegmentwired_1_d), .c(sevensegmentwired_1_c));
  _7_Segment_Display #(.decimalPoint("false")) u_7_segment_display_2 (
    .g(sevensegmentwired_2_g), .f(sevensegmentwired_2_f), .a(sevensegmentwired_2_a),
    .b(sevensegmentwired_2_b), .e(sevensegmentwired_2_e), .d(sevensegmentwired_2_d), .c(sevensegmentwired_2_c));
endmodule
