// Logisim project week3.circ as structural Verilog: 1 circuit, main circuit main
module main (
  input  input_1,
  input  input_2,
  input  input_1_2,
  input  input_2_2,
  input  a,
  input  b,
  input  c,
  input  a_2,
  input  b_2,
  input  c_2,
  output \output ,
  output output_2,
  output f,
  output g
);

  wire and_1_out, and_2_out, and_3_out, and_4_out, and_5_out, and_6_out, not_1_out, not_2_out, not_3_out,
       not_4_out, not_5_out, or_1_out, or_2_out;

  not not_1 (not_1_out, b_2);
  and and_1 (and_1_out, input_1, not_2_out);
  not not_2 (not_2_out, input_2);
  not not_3 (not_3_out, input_1);
  and and_2 (and_2_out, not_3_out, input_2);
  xor xor_1 (output_2, input_1_2, input_2_2);
  or or_1 (or_1_out, a, b);
  not not_4 (not_4_out, a);
  not not_5 (not_5_out, c);
  and and_3 (and_3_out, or_1_out, c);
  and and_4 (and_4_out, not_4_out, b, not_5_out);
  and and_5 (and_5_out, a_2, c_2);
  and and_6 (and_6_out, not_1_out, c_2);
  or or_2 (or_2_out, a_2, not_1_out, c_2);
  or or_3 (\output , and_1_out, and_2_out);
  or or_4 (f, and_3_out, and_4_out);
  or or_5 (g, and_5_out, and_6_out, or_2_out);

  // Notes on the sheet:
  //   a)
  //   b)
  //   XOR-Gate
  //   f = (a + b)c +!ab!c
  //   g = ac + !bc + !ab!c
  //   XOR-Gate
endmodule
