// Logisim project week4.circ as structural Verilog: 1 circuit, main circuit main
module main (
  input  a,
  input  b,
  input  c,
  input  a_2,
  input  b_2,
  input  c_2,
  input  a_3,
  input  b_3,
  input  c_3,
  input  a_4,
  input  b_4,
  input  c_4,
  input  a_5,
  input  b_5,
  input  c_5,
  input  d,
  input  a_6,
  input  b_6,
  input  c_6,
  input  a_7,
  input  b_7,
  input  c_7,
  input  d_2,
  output f,
  output f_2,
  output f_3,
  output f_4,
  output out_28,
  output out_29,
  output out_30
);

  wire and_1_out, and_2_out, and_3_out, and_4_out, and_5_out, and_6_out, and_7_out, and_8_out, and_9_out,
       and_10_out, nand_1_out, nand_2_out, nand_3_out, nand_4_out, nand_5_out, nand_6_out, nand_7_out,
       nand_8_out, nand_9_out, nand_10_out, nand_11_out, nand_12_out, nand_13_out, nand_15_out, nand_16_out,
       nand_17_out, nor_1_out, nor_2_out, nor_3_out, nor_4_out, nor_5_out, nor_6_out, nor_7_out, nor_8_out,
       nor_9_out, nor_10_out, nor_11_out, nor_12_out, nor_13_out, nor_14_out, nor_15_out, nor_17_out,
       nor_18_out, nor_19_out, nor_20_out, not_1_out, not_2_out, not_3_out, not_4_out, not_5_out, or_1_out;

  nor nor_1 (nor_1_out, a_6, a_6);
  nor nor_2 (nor_2_out, b_6, b_6);
  nor nor_3 (nor_3_out, c_6, c_6);
  and and_1 (and_1_out, ~a_2, ~b_2, c_2);  // AND_Gate
  and and_2 (and_2_out, a_2, b_2, ~c_2);  // AND_Gate
  and and_3 (and_3_out, a_2, b_2, c_2);
  and and_4 (and_4_out, ~a_3, ~b_3, c_3);  // AND_Gate
  and and_5 (and_5_out, ~a_3, b_3, c_3);  // AND_Gate
  and and_6 (and_6_out, ~a_3, b_3, ~c_3);  // AND_Gate
  and and_7 (and_7_out, a_3, b_3, c_3);
  nand nand_1 (nand_1_out, a_4, a_4);
  nand nand_2 (nand_2_out, b_4, b_4);
  nand nand_3 (nand_3_out, c_4, c_4);
  nor nor_4 (nor_4_out, b_7, b_7);
  nor nor_5 (nor_5_out, c_7, c_7);
  not not_1 (not_1_out, a);
  and and_8 (and_8_out, not_1_out, b, not_2_out);
  not not_2 (not_2_out, c);
  not not_3 (not_3_out, b);
  and and_9 (and_9_out, a, not_3_out, c);
  and and_10 (and_10_out, a, b, not_4_out);
  not not_4 (not_4_out, c);
  or or_1 (or_1_out, a, b, c);
  or or_2 (f_3, and_4_out, and_5_out, and_6_out, and_7_out);
  nand nand_4 (nand_4_out, a_5, a_5);
  nand nand_5 (nand_5_out, d, d);
  nor nor_6 (nor_6_out, a_7, a_7);
  nor nor_7 (nor_7_out, d_2, d_2);
  not not_5 (not_5_out, or_1_out);
  or or_3 (f_2, and_1_out, and_2_out, and_3_out);
  nand nand_6 (nand_6_out, nand_1_out, nand_2_out, c_4);
  nand nand_7 (nand_7_out, nand_1_out, b_4, nand_3_out);
  nand nand_8 (nand_8_out, a_4, nand_2_out, nand_3_out);
  nand nand_9 (nand_9_out, a_4, b_4, c_4);
  nand nand_10 (nand_10_out, a_5, b_5);
  nand nand_11 (nand_11_out, c_5, d);
  nand nand_12 (nand_12_out, nand_4_out, b_5);
  nand nand_13 (nand_13_out, c_5, nand_5_out);
  nor nor_8 (nor_8_out, a_6, b_6, c_6);
  nor nor_9 (nor_9_out, a_6, nor_2_out, nor_3_out);
  nor nor_10 (nor_10_out, nor_1_out, b_6, nor_3_out);
  nor nor_11 (nor_11_out, nor_1_out, nor_2_out, c_6);
  nor nor_12 (nor_12_out, nor_6_out, nor_4_out);
  nor nor_13 (nor_13_out, nor_5_out, nor_7_out);
  nor nor_14 (nor_14_out, a_7, nor_4_out);
  nor nor_15 (nor_15_out, nor_5_out, d_2);
  or or_4 (f, and_8_out, and_9_out, and_10_out, not_5_out);
  nand nand_14 (f_4, nand_6_out, nand_7_out, nand_8_out, nand_9_out);
  nand nand_15 (nand_15_out, nand_10_out, nand_11_out);
  nand nand_16 (nand_16_out, nand_15_out, nand_15_out);
  nand nand_17 (nand_17_out, nand_12_out, nand_13_out);
  nor nor_16 (out_29, nor_8_out, nor_9_out, nor_10_out, nor_11_out);
  nor nor_17 (nor_17_out, nor_12_out, nor_13_out);
  nor nor_18 (nor_18_out, nor_17_out, nor_17_out);
  nor nor_19 (nor_19_out, nor_14_out, nor_15_out);
  nand nand_18 (out_28, nand_16_out, nand_17_out);
  nor nor_20 (nor_20_out, nor_18_out, nor_19_out);
  nor nor_21 (out_30, nor_20_out, nor_20_out);

  // Notes on the sheet:
  //   1c)
  //   a)i)
  //   a)ii)
  //   b)i)
  //   2a)i)
  //   ii)
  //   2b)i)
  //   ii)
endmodule
