// Logisim project week5.circ as structural Verilog: 1 circuit, main circuit SevenSegmentWired
module SevenSegmentWired (
  input  W,
  input  X,
  input  Y,
  input  Z,
  output a,
  output b,
  output c,
  output d,
  output e,
  output f,
  output g
);

  wire and_1_out, and_2_out, and_3_out, and_4_out, and_5_out, and_6_out, or_1_out, or_2_out, xor_1_out,
       xor_2_out;

  xor xor_1 (xor_1_out, X, Z);
  xor xor_2 (xor_2_out, Y, Z);
  or or_1 (or_1_out, X, Z);
  and and_1 (and_1_out, ~X, Y);  // AND_Gate
  and and_2 (and_2_out, Y, ~Z);  // AND_Gate
  and and_3 (and_3_out, X, ~Y, Z);  // AND_Gate
  or or_2 (or_2_out, Y, Z);
  and and_4 (and_4_out, X, ~Y);  // AND_Gate
  and and_5 (and_5_out, X, ~Z);  // AND_Gate
  and and_6 (and_6_out, ~X, Y);  // AND_Gate
  or or_3 (a, W, Y, ~xor_1_out);  // OR_Gate
  or or_4 (b, ~X, ~xor_2_out);  // OR_Gate
  or or_5 (c, X, ~Y, Z);  // OR_Gate
  or or_6 (d, ~or_1_out, and_1_out, and_2_out, and_3_out, W);  // OR_Gate
  or or_7 (e, ~or_1_out, and_2_out);  // OR_Gate
  or or_8 (f, W, ~or_2_out, and_4_out, and_5_out);  // OR_Gate
  or or_9 (g, W, and_6_out, and_4_out, and_5_out);
  _7_Segment_Display #(.decimalPoint("false")) u_7_segment_display_1 (.g(g), .f(f), .a(a), .b(b), .e(e), .d(d), .c(c));

  // Notes on the sheet:
  //   Seven Segment Display
  //   with improved logic expressions for a-g
endmodule
